// Logisim project lab9.circ as structural Verilog: 2 circuits, main circuit main
module main (
  input  [3:0] Y,
  input  [3:0] X,
  input  Cin,
  output [4:0] S
);

  wire full_adder_1_s, full_adder_2_s, full_adder_3_s;

  Full_Adder full_adder_1 (.X(Y[0]), .Y(X[0]), .Z(Cin), .C(S[0]), .S(full_adder_1_s));
  Full_Adder full_adder_2 (.X(Y[1]), .Y(X[1]), .Z(full_adder_1_s), .C(S[1]), .S(full_adder_2_s));
  Full_Adder full_adder_3 (.X(Y[2]), .Y(X[2]), .Z(full_adder_2_s), .C(S[2]), .S(full_adder_3_s));
  Full_Adder full_adder_4 (.X(Y[3]), .Y(X[3]), .Z(full_adder_3_s), .C(S[3]), .S(S[4]));
endmodule

module Full_Adder (
  input  X,
  input  Y,
  input  Z,
  output C,
  output S
);

  wire and_1_out, and_2_out, xor_1_out;

  xor xor_1 (xor_1_out, X, Y);
  and and_1 (and_1_out, X, Y);
  xor xor_2 (C, xor_1_out, Z);
  and and_2 (and_2_out, xor_1_out, Z);
  or or_1 (S, and_2_out, and_1_out);
endmodule
